# Fritzing sketch schema (saved by Fritzing 0.9.3b)
breadboards: 1

parts:
  Raspberry_Pi_B_rev1 = Raspberry Pi B rev1
  S1 = Pushbutton [package="[THT]"]
  S2 = Pushbutton [package="[THT]"]
  S3 = Pushbutton [package="[THT]"]
  S4 = Pushbutton [package="[THT]"]
  S5 = Pushbutton [package="[THT]"]
  S6 = Pushbutton [package="[THT]"]
  R1 = Resistor [tolerance=±5% resistance=220 package="2010 [SMD]"]
  LED1 = smd LED [color="Red (633nm)" package="0603 [SMD]"]
  R2 = Resistor [tolerance=±5% resistance=220 package="2010 [SMD]"]
  R3 = Resistor [tolerance=±5% resistance=220 package="2010 [SMD]"]
  R4 = Resistor [tolerance=±5% resistance=220 package="2010 [SMD]"]
  R5 = Resistor [tolerance=±5% resistance=220 package="2010 [SMD]"]
  R6 = Resistor [tolerance=±5% resistance=220 package="2010 [SMD]"]
  R7 = Resistor [tolerance=±5% resistance=220 package="2010 [SMD]"]

nets:
  N1: Raspberry_Pi_B_rev1.5V, R2.Pin_0, R3.Pin_0, R4.Pin_0, R5.Pin_0, R6.Pin_0, R7.Pin_0
  N2: Raspberry_Pi_B_rev1.GND, Raspberry_Pi_B_rev1.GPIO_21, S1.Pin_1, S1.Pin_2, S1.Pin_3, S1.Pin_4, S2.Pin_1, S2.Pin_2, S3.Pin_1, S3.Pin_2, S4.Pin_1, S4.Pin_2, S5.Pin_1, S5.Pin_2, S6.Pin_1, S6.Pin_2, LED1.cathode, R2.Pin_1
  N3: Raspberry_Pi_B_rev1.GPIO_23, S2.Pin_3, S2.Pin_4, R3.Pin_1
  N4: Raspberry_Pi_B_rev1.GPIO_17, S6.Pin_3, S6.Pin_4, R7.Pin_1
  N5: Raspberry_Pi_B_rev1.GPIO_18, R1.Pin_1
  N6: Raspberry_Pi_B_rev1.GPIO_22, S5.Pin_3, S5.Pin_4, R6.Pin_1
  N7: Raspberry_Pi_B_rev1.GPIO_24, S3.Pin_3, S3.Pin_4, R4.Pin_1
  N8: Raspberry_Pi_B_rev1.GPIO_25, S4.Pin_3, S4.Pin_4, R5.Pin_1
  N9: R1.Pin_0, LED1.anode

notes:
  left
  up
  down
  vol-
  vol+
  right
  1K
  10K
